// Logisim project Real_Alu.circ as structural Verilog: 8 circuits, main circuit main
module main (
);

  decoder decoder_1 ();  // open: S3, S2, S1, S0, out_5
endmodule

module Mux_4bit (
  input  [3:0] S,
  input  _0,
  input  _1,
  input  _2,
  input  _3,
  input  _4,
  input  _5,
  input  _6,
  input  _7,
  input  _8,
  input  _9,
  input  _10,
  input  _11,
  input  _12,
  input  _13,
  input  _14,
  input  _15,
  output out_18
);

  wire _0_t, _1_t, _2_t, _3_t, _4_t, _5_t, _6_t, _7_t, _8_t, _9_t, _10_t, _11_t, _12_t, _13_t, _14_t, _15_t,
       S00, S11, S22, S33;

  not not_1 (S22, S[2]);
  not not_2 (S33, S[3]);
  not not_3 (S00, S[0]);
  not not_4 (S11, S[1]);
  and and_1 (_0_t, S00, S11, S22, S33, _0);
  and and_2 (_1_t, S[0], S11, S22, S33, _1);
  and and_3 (_2_t, S00, S[1], S22, S33, _2);
  and and_4 (_3_t, S[0], S[1], S22, S33, _3);
  and and_5 (_4_t, S00, S11, S[2], S33, _4);
  and and_6 (_5_t, S[0], S11, S[2], S33, _5);
  and and_7 (_6_t, S00, S[1], S[2], S33, _6);
  and and_8 (_7_t, S[0], S[1], S[2], S33, _7);
  and and_9 (_8_t, S00, S11, S22, S[3], _8);
  and and_10 (_9_t, S[0], S11, S22, S[3], _9);
  and and_11 (_10_t, S00, S[1], S22, S[3], _10);
  and and_12 (_11_t, S[0], S[1], S22, S[3], _11);
  and and_13 (_12_t, S00, S11, S[2], S[3], _12);
  and and_14 (_13_t, S[0], S11, S[2], S[3], _13);
  and and_15 (_14_t, S00, S[1], S[2], S[3], _14);
  and and_16 (_15_t, S[0], S[1], S[2], S[3], _15);
  or or_1 (out_18, _0_t, _1_t, _2_t, _3_t, _4_t, _5_t, _6_t, _7_t, _8_t, _9_t, _10_t, _11_t, _12_t, _13_t, _14_t, _15_t);
endmodule

module And (
  input  Enable,
  input  [7:0] a,
  input  [7:0] b,
  output [7:0] out_4,
  output z
);

  wire nor_1_out;
  wire [7:0] and_1_out;

  assign and_1_out = a & b;  // AND_Gate and_1, 8 bits wide
  nor nor_1 (nor_1_out, and_1_out[7], and_1_out[6], and_1_out[5], and_1_out[4], and_1_out[3], and_1_out[2], and_1_out[1], and_1_out[0]);
  and and_2 (z, nor_1_out, Enable);
  assign out_4 = {8{Enable}} & and_1_out;  // AND_Gate and_3, 8 bits wide

  // Other names for the same wires on the sheet: e = Enable
endmodule

module Or (
  input  Enable,
  input  [7:0] a,
  input  [7:0] b,
  output [7:0] out_4,
  output z
);

  wire nor_1_out;
  wire [7:0] or_1_out;

  assign or_1_out = a | b;  // OR_Gate or_1, 8 bits wide
  nor nor_1 (nor_1_out, or_1_out[7], or_1_out[6], or_1_out[5], or_1_out[4], or_1_out[3], or_1_out[2], or_1_out[1], or_1_out[0]);
  assign out_4 = {8{Enable}} & or_1_out;  // AND_Gate and_1, 8 bits wide
  and and_2 (z, nor_1_out, Enable);

  // Other names for the same wires on the sheet: e = Enable
endmodule

module Not_B (
  input  Enable,
  input  [7:0] B,
  output [7:0] out_3,
  output z
);

  wire nor_1_out;
  wire [7:0] not_1_out;

  assign not_1_out = ~B;  // NOT_Gate not_1, 8 bits wide
  nor nor_1 (nor_1_out, not_1_out[7], not_1_out[6], not_1_out[5], not_1_out[4], not_1_out[3], not_1_out[2], not_1_out[1], not_1_out[0]);
  assign out_3 = {8{Enable}} & not_1_out;  // AND_Gate and_1, 8 bits wide
  and and_2 (z, nor_1_out, Enable);

  // Other names for the same wires on the sheet: e = Enable
endmodule

module LSR_B (
  input  Enable,
  input  [7:0] B,
  output [7:0] out_3,
  output Carry,
  output Z,
  output P_N
);

  wire nor_1_out;

  nor nor_1 (nor_1_out, B[0], B[1], B[2], B[3], B[4], B[5], B[6], B[7]);
  and and_1 (Carry, B[7], Enable);
  and and_2 (Z, Enable, nor_1_out);
  assign out_3 = {8{Enable}} & {B[6:0], 1'b0};  // AND_Gate and_3, 8 bits wide
  and and_4 (P_N, B[7], Enable);

  // Other names for the same wires on the sheet: e = Enable
endmodule

module LSL_B (
  input  Enable,
  input  [7:0] B,
  output [7:0] out_3,
  output Carry,
  output Z,
  output P_N
);

  wire nor_1_out;

  nor nor_1 (nor_1_out, B[0], B[1], B[2], B[3], B[4], B[5], B[6], B[7]);
  and and_1 (Carry, Enable, B[0]);
  and and_2 (P_N, B[7], Enable);
  and and_3 (Z, Enable, nor_1_out);
  and and_4 (out_3[0], Enable, B[1]);
  and and_5 (out_3[1], Enable, B[2]);
  and and_6 (out_3[2], Enable, B[3]);
  and and_7 (out_3[3], Enable, B[4]);
  and and_8 (out_3[4], Enable, B[5]);
  and and_9 (out_3[5], Enable, B[6]);
  and and_10 (out_3[6], Enable, B[7]);
  and and_11 (out_3[7], Enable, 1'b0);
  // AND_Gate and_12 is placed but not wired

  // Other names for the same wires on the sheet: e = Enable
endmodule

module decoder (
  input  S3,
  input  S2,
  input  S1,
  input  S0,
  output [15:0] out_5
);

  wire not_1_out, not_2_out, not_3_out, not_4_out;

  not not_1 (not_1_out, S1);
  not not_2 (not_2_out, S2);
  not not_3 (not_3_out, S3);
  not not_4 (not_4_out, S0);
  and and_1 (out_5[0], not_4_out, not_1_out, not_2_out, not_3_out);
  and and_2 (out_5[1], S0, not_1_out, not_2_out, not_3_out);
  and and_3 (out_5[2], not_4_out, S1, not_2_out, not_3_out);
  and and_4 (out_5[3], S0, S1, not_2_out, not_3_out);
  and and_5 (out_5[4], not_4_out, not_1_out, S2, not_3_out);
  and and_6 (out_5[5], S0, not_1_out, S2, not_3_out);
  and and_7 (out_5[6], not_4_out, S1, S2, not_3_out);
  and and_8 (out_5[7], S0, S1, S2, not_3_out);
  and and_9 (out_5[8], not_4_out, not_1_out, not_2_out, S3);
  and and_10 (out_5[9], S0, not_1_out, not_2_out, S3);
  and and_11 (out_5[10], not_4_out, S1, not_2_out, S3);
  and and_12 (out_5[11], S0, S1, not_2_out, S3);
  and and_13 (out_5[12], not_4_out, not_1_out, S2, S3);
  and and_14 (out_5[13], S0, not_1_out, S2, S3);
  and and_15 (out_5[14], not_4_out, S1, S2, S3);
  and and_16 (out_5[15], S0, S1, S2, S3);
endmodule
